// Logisim project control.circ as structural Verilog: 1 circuit, main circuit main
// Control Unit
module main (
  input  CLK,
  input  [3:0] Cond,
  input  [1:0] Op,
  input  [5:0] Funct,
  input  [3:0] Rd,
  input  [3:0] ALUFlags,
  input  [1:0] sh,
  output PCSrc,
  output RegWrite,
  output MemWrite,
  output MemtoReg,
  output ALUSrc,
  output [1:0] ImmSrc,
  output [1:0] RegSrc,
  output [3:0] ALUControl
);

  wire AL_out, ALUOp, and_2_out, and_3_out, C, comparator_1_eq, CondEx, decoder_1_out0, decoder_1_out1,
       decoder_1_out10, decoder_1_out11, decoder_1_out12, decoder_1_out13, decoder_1_out14, EQ_out, GE_out,
       GT_out, LE_out, LT_out, MemW, NE_out, not_1_out, not_2_out, not_3_out, not_5_out, not_6_out,
       not_7_out, NoWrite, or_1_out, or_2_out, or_6_out, PCS, RegW, xor_1_out;
  wire [0:0] Flags1_0;
  wire [1:0] and_4_out, Flags3_2, FlagW, multiplexer_1_out, multiplexer_2_out;
  wire [1:1] undriven;

  not not_1 (not_1_out, Op[1]);
  or or_1 (or_1_out, Op[1], Op[0]);
  or or_2 (or_2_out, Op[1], Op[0]);
  or or_3 (ALUSrc, Op[1], Funct[5], Op[0]);
  and and_1 (MemW, Op[0], not_2_out);
  not not_2 (not_2_out, Funct[0]);
  and and_2 (and_2_out, Funct[0], not_1_out);
  or or_4 (RegW, and_2_out, not_3_out);
  not not_3 (not_3_out, or_1_out);
  not not_4 (ALUOp, or_2_out);
  Comparator #(.width(4)) comparator_1 (.a(Rd), .b(4'b1111), .eq(comparator_1_eq));  // open: gt, lt
  Multiplexer #(.select(4), .width(2), .enable("false")) multiplexer_1 (
    .in0(2'b10), .in1(2'b10), .in2(2'b11), .in4(2'b11), .in10(2'b11), .in12(2'b10), .in13(2'b10),
    .out(multiplexer_1_out), .sel(Funct[4:1]));  // open: in3, in5, in6, in7, in8, in9, in11, in14, in15
  and and_3 (and_3_out, comparator_1_eq, RegW);
  Multiplexer #(.width(2), .enable("false")) multiplexer_2 (
    .in0(2'b00), .in1(multiplexer_1_out), .out(multiplexer_2_out), .sel(Funct[0]));
  Comparator #(.width(4)) comparator_2 (.a(4'b1010), .b(Funct[4:1]), .eq(NoWrite));  // open: gt, lt
  alu_control_main main_1 (.Opcode(Op), .Funct(Funct), .sh(sh), .ALUControl(ALUControl));
  or or_5 (PCS, and_3_out, Op[1]);
  Multiplexer #(.width(2), .enable("false")) multiplexer_3 (
    .in0(2'b00), .in1(multiplexer_2_out), .out(FlagW), .sel(ALUOp));
  Decoder #(.select(4), .enable("false")) decoder_1 (
    .out0(decoder_1_out0), .out1(decoder_1_out1), .out10(decoder_1_out10), .out11(decoder_1_out11),
    .out12(decoder_1_out12), .out13(decoder_1_out13), .out14(decoder_1_out14), .sel(Cond));  // open: out2, out3, out4, out5, out6, out7, out8, out9, out15
  Register #(.width(2)) register_1 (.D(ALUFlags[3:2]), .Q(Flags3_2), .clk(CLK), .clr(and_4_out[1]));  // open: en
  Register #(.width(2)) register_2 (
    .D(ALUFlags[1:0]), .Q({C, Flags1_0[0]}), .clk(CLK), .clr(and_4_out[0]));  // open: en
  not not_5 (not_5_out, Flags3_2[0]);
  assign and_4_out = FlagW & {undriven[1], CondEx};  // AND_Gate and_4, 2 bits wide
  and EQ (EQ_out, Flags3_2[0], decoder_1_out0);
  and NE (NE_out, decoder_1_out1, not_5_out);
  xor xor_1 (xor_1_out, Flags1_0[0], Flags3_2[1]);
  not not_6 (not_6_out, NoWrite);
  not not_7 (not_7_out, xor_1_out);
  and LT (LT_out, decoder_1_out11, xor_1_out);
  or or_6 (or_6_out, xor_1_out, Flags3_2[0]);
  and and_5 (PCSrc, PCS, CondEx);
  and and_6 (RegWrite, RegW, not_6_out, CondEx);
  and and_7 (MemWrite, MemW, CondEx);
  and GE (GE_out, not_7_out, decoder_1_out10);
  and GT (GT_out, not_7_out, decoder_1_out12, not_5_out);
  and LE (LE_out, decoder_1_out13, or_6_out);
  buf AL (AL_out, decoder_1_out14);
  or or_7 (CondEx, EQ_out, NE_out, GE_out, LT_out, GT_out, LE_out, AL_out);

  assign ImmSrc = Op;
  assign MemtoReg = Op[0];
  assign RegSrc = {Op[0], Op[1]};

  // Other names for the same wires on the sheet: V = Flags1_0[0]; Flags1_0[1] = C; Z = Flags3_2[0]; N = Flags3_2[1];
  //   S = Funct[0]; I = Funct[5]; Branch = Op[1]

  // Notes on the sheet:
  //   Main Decoder
  //   Hongwei Cai
  //   ARM Processor
  //   Computer Organization
  //   Spring 2022
  //   PC Logic
  //   ALU Decoder
  //   Z|(NxorV)
  //   Conditional Logic
  //   Condition Check
  //   NxorV
  //   ~(NxorV)
  //   ~Z&~(NxorV)
endmodule
