// Logisim project iodevices.circ as structural Verilog: 1 circuit, main circuit main
module main (
  input  in_1,
  input  [31:0] Address,
  input  WrEn,
  input  [31:0] WriteData
);

  wire and_1_out, clock_1_out, comparator_1_eq, register_1_q;

  Comparator #(.width(32)) comparator_1 (.a(Address), .b(32'h7f00), .eq(comparator_1_eq));  // open: gt, lt
  and and_1 (and_1_out, comparator_1_eq, WrEn);
  Clock clock_1 (.out(clock_1_out));
  TTY tty_1 ();  // open: data, clk, we, clr
  Register #(.width(1)) register_1 (
    .D(WriteData[0]), .en(and_1_out), .Q(register_1_q), .clk(clock_1_out));  // open: clr
  LED led_1 ();  // open: in
  DotMatrix #(.matrixcols(7), .matrixrows(1)) dotmatrix_1 ();  // open: col0, col1, col2, col3, col4, col5, col6
  _7_Segment_Display u_7_segment_display_1 ();  // open: g, f, a, b, e, d, c, dp
  Keyboard keyboard_1 ();  // open: clk, re, clr, avail, data
  Button button_1 ();  // open: out
  Hex_Digit_Display hex_digit_display_1 ();  // open: value, dp
  Joystick joystick_1 ();  // open: x, y

  // Other names for the same wires on the sheet: CLK = in_1

  // Notes on the sheet:
  //   This IO device is an LED. If you write a 1 to its address (0x00007F00) then it will turn on.
  //   check for 0x00007F00
  //   The clock is here for illustration purposes. You should use the same clock as your CPU.
  //   Writing to the LED requires that WrEn=1 and the address is the correct address
  //   register stores data you want to display as output
endmodule
