// Logisim project alu.circ as structural Verilog: 1 circuit, main circuit main
module main (
  input  [31:0] A,
  input  [31:0] B,
  input  [3:0] ALUControl,
  output [3:0] ALUFlags,
  output [31:0] Result
);

  wire adder_1_cout, adder_2_cout, and_2_out, and_3_out, comparator_2_eq, comparator_3_eq, not_3_out,
       or_2_out, or_4_out, xor_2_out, xor_3_out, xor_4_out;
  wire [31:0] add, \and , asr, lsl, lsr, \not , not_1_out, \or , sub, \xor ;

  Multiplexer #(.select(4), .width(32), .enable("false")) multiplexer_1 (
    .in0(\and ), .in1(\or ), .in2(\xor ), .in3(\not ), .in4(lsl), .in5(lsr), .in6(asr), .in7(add), .in8(sub),
    .in13(B), .out(Result), .sel(ALUControl));  // open: in9, in10, in11, in12, in14, in15
  Comparator #(.width(32)) comparator_1 (.a(Result), .b({32{1'b0}}), .eq(ALUFlags[2]), .lt(ALUFlags[3]));  // open: gt
  assign not_1_out = ~B;  // NOT_Gate not_1, 32 bits wide
  assign \and  = A & B;  // AND_Gate and_1, 32 bits wide
  assign \or  = A | B;  // OR_Gate or_1, 32 bits wide
  assign \xor  = A ^ B;  // XOR_Gate xor_1, 32 bits wide
  assign \not  = ~A;  // NOT_Gate not_2, 32 bits wide
  Shifter #(.width(32)) shifter_1 (.in(B), .\dist (A[4:0]), .out(lsl));
  Shifter #(.width(32), .shift("lr")) shifter_2 (.in(B), .\dist (A[4:0]), .out(lsr));
  Shifter #(.width(32), .shift("ar")) shifter_3 (.in(B), .\dist (A[4:0]), .out(asr));
  Adder #(.width(32)) adder_1 (.a(A), .b(B), .out(add), .cout(adder_1_cout));  // open: cin
  Comparator #(.width(4)) comparator_2 (.a(4'b0111), .b(ALUControl), .eq(comparator_2_eq));  // open: gt, lt
  Adder #(.width(32)) adder_2 (.a(A), .b(not_1_out), .out(sub), .cin(1'b1), .cout(adder_2_cout));
  Comparator #(.width(4)) comparator_3 (.a(4'b1000), .b(ALUControl), .eq(comparator_3_eq));  // open: gt, lt
  or or_2 (or_2_out, comparator_2_eq, comparator_3_eq);
  xor xor_2 (xor_2_out, A[31], Result[31]);
  and and_2 (and_2_out, adder_1_cout, comparator_2_eq);
  and and_3 (and_3_out, adder_2_cout, comparator_3_eq);
  ExactlyOne xor_3 (.out(xor_3_out), .in0(A[31]), .in1(B[31]), .in2(comparator_2_eq));
  not not_3 (not_3_out, A[31]);
  ExactlyOne xor_4 (.out(xor_4_out), .in0(not_3_out), .in1(B[31]), .in2(comparator_3_eq));
  or or_3 (ALUFlags[1], and_2_out, and_3_out);
  or or_4 (or_4_out, xor_3_out, xor_4_out);
  and and_4 (ALUFlags[0], or_4_out, or_2_out, xor_2_out);

  // Other names for the same wires on the sheet: oVerflow = ALUFlags[0]; Carry = ALUFlags[1]; Zero = ALUFlags[2];
  //   Negative = ALUFlags[3]; Ctrl[3:0] = ALUControl

  // Notes on the sheet:
  //   INPUTS to your circuit
  //   DON'T CHANGE THE LOCATIONS OF THE INPUTS AND OUTPUTS!
  //   Spring 2022
  //   OUTPUTS from your circuit
  //   Hongwei Cai
  //   ARM Processor
  //   Computer Organization
endmodule
