// Logisim project cond-add-sub.circ as structural Verilog: 1 circuit, main circuit main
module main (
  output [31:0] R0_Value,
  output [31:0] R1_Value,
  output [31:0] R2_Value,
  output [31:0] LR__R14__Value,
  output [31:0] SP__R13__Value,
  output [31:0] Time_Step,
  output [31:0] Requested_Address,
  output [31:0] Requested_Instruction,
  output halt
);

  wire clock_1_out;

  Clock clock_1 (.out(clock_1_out));
  cpu_main main_1 (
    .INSTRUCTION(Requested_Instruction), .CLOCK(clock_1_out), .FETCH_ADDRESS(Requested_Address),
    .R0_Value(R0_Value), .R1_Value(R1_Value), .R2_Value(R2_Value), .LR_Value(LR__R14__Value),
    .SP_Value(SP__R13__Value));
  Counter #(.width(32), .max('hffffffff)) counter_1 (
    .Q(Time_Step), .clk(clock_1_out));  // open: load, D, count, carry, clr
  Comparator #(.width(32)) comparator_1 (.a(Time_Step), .b(32'h8), .eq(halt));  // open: gt, lt
  // Probe on Requested_Address
  ROM #(.addrWidth(24), .dataWidth(32)) rom_1 (
    .addr(Requested_Address[25:2]), .data(Requested_Instruction));  // open: sel
  // Probe on Requested_Instruction

  // Other names for the same wires on the sheet: fetch_addr[31:0] = Requested_Address;
  //   Instruction[31:0] = Requested_Instruction

  // Notes on the sheet:
  //   YOUR CPU SHOULD FIT IN HERE!
  //   When copying this template, the only modifications you should make are
  //   2. load the instruction memory ROM with the machine code of your program
  //   1. set the constant going into the comparator to be larger than the number of clock periods you need for the program to finish
  //   Instruction Memory
  //   contents of rom_1 (hex, n*v repeats v):
  //   e3a00064 e3a01032 e1500001 802001 10402001 e1510002 410002 10810002
endmodule
