// Logisim project cond-add.circ as structural Verilog: 1 circuit, main circuit main
module main (
  output [31:0] s0_Value,
  output [31:0] s1_Value,
  output [31:0] s2_Value,
  output [31:0] LR__R14__Value,
  output [31:0] SP__R13__Value,
  output [31:0] Time_Step,
  output halt
);

  wire clock_1_out;
  wire [31:0] fetch_addr, Instruction;

  Clock clock_1 (.out(clock_1_out));
  cpu_main main_1 (
    .INSTRUCTION(Instruction), .CLOCK(clock_1_out), .FETCH_ADDRESS(fetch_addr), .R0_Value(s0_Value),
    .R1_Value(s1_Value), .R2_Value(s2_Value), .LR_Value(LR__R14__Value), .SP_Value(SP__R13__Value));
  Counter #(.width(32), .max('hffffffff)) counter_1 (
    .Q(Time_Step), .clk(clock_1_out));  // open: load, D, count, carry, clr
  Comparator #(.width(32)) comparator_1 (.a(Time_Step), .b(32'h8), .eq(halt));  // open: gt, lt
  // Probe on fetch_addr
  ROM #(.addrWidth(24), .dataWidth(32)) rom_1 (.addr(fetch_addr[25:2]), .data(Instruction));  // open: sel
  // Probe on Instruction

  // Notes on the sheet:
  //   YOUR CPU SHOULD FIT IN HERE!
  //   When copying this template, the only modifications you should make are
  //   2. load the instruction memory ROM with the machine code of your program
  //   1. set the constant going into the comparator to be larger than the number of clock periods you need for the program to finish
  //   Instruction Memory
  //   contents of rom_1 (hex, n*v repeats v):
  //   e3a0000b e3a01016 e1500001 e3a00016 802001 10800001
endmodule
