// Logisim project cpu.circ as structural Verilog: 1 circuit, main circuit main
module main (
  input  [31:0] INSTRUCTION,
  input  CLOCK,
  output [31:0] FETCH_ADDRESS,
  output [31:0] R0_Value,
  output [31:0] R1_Value,
  output [31:0] R2_Value,
  output [31:0] LR_Value,
  output [31:0] SP_Value
);

  wire ALUSrc, comparator_1_eq, comparator_2_gt, MemtoReg, MemWrite, PCSrc, RegWrite;
  wire [1:0] ImmSrc, RegSrc;
  wire [3:0] ALUControl, ALUFlags, multiplexer_2_out, multiplexer_3_out;
  wire [4:0] bit_extender_5_out, shifter_2_out;
  wire [31:0] adder_1_out, adder_3_out, Data_Memory_read_data, DPImm, ExtImm8, ExtImm12, ExtImm24, ExtShamt5,
       main_1_read_data_1, main_3_result, multiplexer_1_out, multiplexer_4_out, multiplexer_5_out,
       multiplexer_6_out, PC, RD2, shifter_1_out, shifter_3_out, WD;

  Multiplexer #(.width(32), .enable("false")) multiplexer_1 (
    .in0(adder_1_out), .in1(WD), .out(multiplexer_1_out), .sel(PCSrc));
  Register #(.width(32)) u_PC (.D(multiplexer_1_out), .Q(FETCH_ADDRESS), .clk(CLOCK));  // open: en, clr
  assign ExtShamt5 = {{27{1'b0}}, INSTRUCTION[11:7]};  // Bit_Extender bit_extender_1
  assign ExtImm8 = {{24{1'b0}}, INSTRUCTION[7:0]};  // Bit_Extender bit_extender_2
  assign ExtImm12 = {{20{1'b0}}, INSTRUCTION[11:0]};  // Bit_Extender bit_extender_3
  assign ExtImm24 = {{8{INSTRUCTION[23]}}, INSTRUCTION[23:0]};  // Bit_Extender bit_extender_4
  Adder #(.width(32)) adder_1 (.a(FETCH_ADDRESS), .b(32'h4), .out(adder_1_out));  // open: cin, cout
  Adder #(.width(32)) adder_2 (.a(adder_1_out), .b(32'h4), .out(PC));  // open: cin, cout
  Multiplexer #(.width(4), .enable("false")) multiplexer_2 (
    .in0(INSTRUCTION[19:16]), .in1(4'b1111), .out(multiplexer_2_out), .sel(RegSrc[1]));
  Multiplexer #(.width(4), .enable("false")) multiplexer_3 (
    .in0(INSTRUCTION[3:0]), .in1(INSTRUCTION[15:12]), .out(multiplexer_3_out), .sel(RegSrc[0]));
  Shifter #(.width(32)) shifter_1 (.in(ExtImm24), .\dist (5'b00010), .out(shifter_1_out));
  Adder #(.width(32)) adder_3 (.a(shifter_1_out), .b(32'h8), .out(adder_3_out));  // open: cin, cout
  regfile_main main_1 (
    .Read_Register_1(multiplexer_2_out), .Read_Register_2(multiplexer_3_out),
    .Write_Register(INSTRUCTION[15:12]), .Write_Data(WD), .Write_Enable(RegWrite), .Clock(CLOCK),
    .Read_Data_1(main_1_read_data_1), .Read_Data_2(RD2), .R0_Value(R0_Value), .R1_Value(R1_Value),
    .R3_Value(R2_Value), .LR__R14__Value(LR_Value), .SP__R13__Value(SP_Value), .R15(PC));
  Multiplexer #(.select(2), .width(32), .enable("false")) multiplexer_4 (
    .in0(DPImm), .in1(ExtImm12), .in2(adder_3_out), .out(multiplexer_4_out), .sel(ImmSrc));  // open: in3
  Multiplexer #(.width(32), .enable("false")) multiplexer_5 (
    .in0(RD2), .in1(multiplexer_4_out), .out(multiplexer_5_out), .sel(ALUSrc));
  control_main main_2 (
    .Cond(INSTRUCTION[31:28]), .Op(INSTRUCTION[27:26]), .Rd(INSTRUCTION[15:12]), .ALUFlags(ALUFlags),
    .CLK(CLOCK), .sh(INSTRUCTION[6:5]), .Funct(INSTRUCTION[25:20]), .PCSrc(PCSrc), .RegWrite(RegWrite),
    .MemWrite(MemWrite), .MemtoReg(MemtoReg), .ALUSrc(ALUSrc), .ImmSrc(ImmSrc), .RegSrc(RegSrc),
    .ALUControl(ALUControl));
  assign bit_extender_5_out = {{1{1'b0}}, INSTRUCTION[11:8]};  // Bit_Extender bit_extender_5
  Multiplexer #(.width(32), .enable("false")) multiplexer_6 (
    .in0(main_1_read_data_1), .in1(ExtShamt5), .out(multiplexer_6_out), .sel(comparator_1_eq));
  Comparator #(.width(5)) comparator_1 (.a(INSTRUCTION[25:21]), .b(5'b01101), .eq(comparator_1_eq));  // open: gt, lt
  Shifter #(.width(5)) shifter_2 (.in(bit_extender_5_out), .\dist (3'b001), .out(shifter_2_out));
  alu_main main_3 (
    .ALUControl(ALUControl), .A(multiplexer_6_out), .ALUFlags(ALUFlags), .Result(main_3_result),
    .B(multiplexer_5_out));
  Multiplexer #(.width(32), .enable("false")) multiplexer_7 (
    .in0(ExtImm8), .in1(shifter_3_out), .out(DPImm), .sel(comparator_2_gt));
  Shifter #(.width(32), .shift("rr")) shifter_3 (.in(ExtImm8), .\dist (shifter_2_out), .out(shifter_3_out));
  Comparator #(.width(4), .mode("unsigned")) comparator_2 (
    .a(INSTRUCTION[11:8]), .b(4'b0000), .gt(comparator_2_gt));  // open: eq, lt
  Multiplexer #(.width(32), .enable("false")) multiplexer_8 (
    .in0(main_3_result), .in1(Data_Memory_read_data), .out(WD), .sel(MemtoReg));
  mem_main Data_Memory (
    .Address(main_3_result), .Write_Data(RD2), .Write_En(MemWrite), .Clock(CLOCK),
    .Read_Data(Data_Memory_read_data));

  // Other names for the same wires on the sheet: clk = CLOCK; fetch_addr[31:0] = FETCH_ADDRESS;
  //   Rm[3:0] = INSTRUCTION[3:0]; sh[1:0] = INSTRUCTION[6:5]; rot[3:0] = INSTRUCTION[11:8];
  //   Rd[3:0] = INSTRUCTION[15:12]; Rn[3:0] = INSTRUCTION[19:16]; Funct[5:0] = INSTRUCTION[25:20];
  //   Op[1:0] = INSTRUCTION[27:26]; Cond[3:0] = INSTRUCTION[31:28]; R0[31:0] = R0_Value; R1[31:0] = R1_Value;
  //   R2[31:0] = R2_Value; R13[31:0] = SP_Value; R14[31:0] = LR_Value

  // Notes on the sheet:
  //   Instruction Memory
  //   Output
  //   DataProcess
  //   MemoryInstr
  //   Branch
  //   PC+4
  //   Inputs
  //   PC+8
  //   These are DEBUG/TEST outputs from your circuit.
  //   Hongwei Cai
  //   ARM Processor
  //   Spring 2022
  //   Computer Organization
endmodule
